// Logisim project circuito.circ as structural Verilog: 1 circuit, main circuit main
module main (
  input  [7:0] Dado,
  input  Clk,
  input  Rst,
  input  WrState,
  input  WrStateSize,
  input  WrTextSize,
  input  WrKeyStream,
  input  Wr_J,
  input  Wr_I,
  input  Wr_K,
  input  Wr_temp,
  input  [7:0] Data_in,
  input  WrData_in,
  input  [1:0] Msoma1,
  input  Msoma2,
  output Status
);

  wire rst_t;
  wire [7:0] adder_1_out, adder_2_out, divider_1_out, divider_1_rem, keyStream, multiplexer_1_out,
       multiplexer_2_out, multiplexer_3_out, multiplexer_4_out, RegData_in_q, RegI_q, RegJ_q, RegK_q,
       RegTemp_q, state, stateSize, texteSize;

  Register RegJ (.D(divider_1_rem), .en(Wr_J), .Q(RegJ_q), .clk(Clk), .clr(rst_t));
  Register RegState (.D(Dado), .en(WrState), .Q(state), .clk(Clk), .clr(rst_t));
  Register RegData_in (.D(Data_in), .en(WrData_in), .Q(RegData_in_q), .clk(Clk), .clr(rst_t));
  Register RegI (.D(divider_1_rem), .en(Wr_I), .Q(RegI_q), .clk(Clk), .clr(rst_t));
  Register RegStateSize (.D(Dado), .en(WrStateSize), .Q(stateSize), .clk(Clk), .clr(rst_t));
  Register RegK (.D(adder_1_out), .en(Wr_K), .Q(RegK_q), .clk(Clk), .clr(rst_t));
  Multiplexer #(.select(2), .width(8), .enable("false")) multiplexer_1 (
    .in0(RegI_q), .in1(RegJ_q), .in2(RegTemp_q), .in3(RegK_q), .out(multiplexer_1_out), .sel(Msoma1));
  Multiplexer #(.select(2), .width(8), .enable("false")) multiplexer_2 (
    .in0(8'h1), .in1(RegData_in_q), .in2(RegData_in_q), .in3(8'h1), .out(multiplexer_2_out), .sel(Msoma1));
  Adder adder_1 (.a(multiplexer_1_out), .b(multiplexer_2_out), .out(adder_1_out));  // open: cin, cout
  Register RegTextSize (.D(Dado), .en(WrTextSize), .Q(texteSize), .clk(Clk), .clr(rst_t));
  Register RegTemp (.en(Wr_temp), .Q(RegTemp_q), .clk(Clk), .clr(rst_t));  // open: D
  Divider divider_1 (.a(adder_1_out), .b(stateSize), .out(divider_1_out), .rem(divider_1_rem));  // open: upper
  Register RegKeyStream (.D(Dado), .en(WrKeyStream), .Q(keyStream), .clk(Clk), .clr(rst_t));
  Comparator comparator_1 (.a(RegK_q), .b(adder_2_out), .lt(Status));  // open: gt, eq
  Multiplexer #(.width(8), .enable("false")) multiplexer_3 (
    .in0(divider_1_out), .in1(texteSize), .out(multiplexer_3_out), .sel(Msoma2));
  Multiplexer #(.width(8), .enable("false")) multiplexer_4 (
    .in0(state), .in1(keyStream), .out(multiplexer_4_out), .sel(Msoma2));
  Adder adder_2 (.a(multiplexer_3_out), .b(multiplexer_4_out), .out(adder_2_out));  // open: cin, cout
  Register RegData_out ();  // open: D, en, Q, clk, clr
  Register RegAddress ();  // open: D, en, Q, clk, clr
endmodule
